// Logisim project alu.circ as structural Verilog: 3 circuits, main circuit alu
module alu (
  input  [31:0] A,
  input  [31:0] B,
  input  [3:0] ALUSel,
  input  [3:0] in_4,
  input  [3:0] in_5,
  input  [3:0] in_6,
  input  [3:0] in_7,
  output [31:0] Result,
  output [3:0] out_9,
  output [3:0] out_10,
  output [3:0] out_11,
  output [3:0] out_12
);

  wire subtractor_1_bout;
  wire [3:0] multiplexer_3_out, multiplexer_4_out, multiplier_2_cout, subtractor_4_out;
  wire [31:0] add, andOut, divOut, lshiftOut, mulhOut, mulhuOut, multiplexer_1_out, multiplexer_2_out,
       multiplier_1_cout, multOut, orOut, rashiftOut, remOut, reverse_1_out_2, reverse_2_out_2, rshiftOut,
       shift_2_out_4, shift_3_out_4, sltOut, subOut, subtractor_2_out, xorOut;

  reverse reverse_1 (.in_1(A), .out_2(reverse_1_out_2));
  reverse reverse_2 (.in_1(A), .out_2(reverse_2_out_2));
  Adder #(.width(32)) adder_1 (.a(A), .b(B), .out(add));  // open: cin, cout
  assign andOut = A & B;  // AND_Gate and_1, 32 bits wide
  assign orOut = A | B;  // OR_Gate or_1, 32 bits wide
  assign xorOut = A ^ B;  // XOR_Gate xor_1, 32 bits wide
  shift shift_1 (.in_1(B), .in_2(A), .in_3(1'b0), .out_4(lshiftOut));
  Subtractor #(.width(32)) subtractor_1 (.a(A), .b(B), .bin(1'b0), .bout(subtractor_1_bout));  // open: out
  Multiplier #(.width(32)) multiplier_1 (.a(A), .b(B), .out(multOut), .cout(multiplier_1_cout));  // open: cin
  shift shift_2 (.in_1(B), .in_2(reverse_1_out_2), .in_3(1'b0), .out_4(shift_2_out_4));
  shift shift_3 (.in_1(B), .in_2(reverse_2_out_2), .in_3(A[31]), .out_4(shift_3_out_4));
  assign sltOut = {{31{subtractor_1_bout}}, subtractor_1_bout};  // Bit_Extender bit_extender_1
  Multiplexer #(.width(32), .enable("false")) multiplexer_1 (
    .in0({32{1'b0}}), .in1(B), .out(multiplexer_1_out), .sel(A[31]));
  reverse reverse_3 (.in_1(shift_2_out_4), .out_2(rshiftOut));
  reverse reverse_4 (.in_1(shift_3_out_4), .out_2(rashiftOut));
  Subtractor #(.width(32)) subtractor_2 (
    .a(multiplier_1_cout), .b(multiplexer_1_out), .out(subtractor_2_out));  // open: bin, bout
  Subtractor #(.width(32)) subtractor_3 (
    .a(subtractor_2_out), .b(multiplexer_2_out), .out(mulhOut));  // open: bin, bout
  Multiplexer #(.width(32), .enable("false")) multiplexer_2 (
    .in0({32{1'b0}}), .in1(A), .out(multiplexer_2_out), .sel(B[31]));
  Multiplier #(.width(4)) multiplier_2 (.a(in_6), .b(in_7), .out(out_11), .cout(multiplier_2_cout));  // open: cin
  Multiplexer #(.width(4), .enable("false")) multiplexer_3 (
    .in0(4'b0000), .in1(in_7), .out(multiplexer_3_out), .sel(in_6[3]));
  Multiplier #(.width(4)) multiplier_3 (.a(in_4), .b(in_5), .out(out_9), .cout(out_10));  // open: cin
  Subtractor #(.width(4)) subtractor_4 (
    .a(multiplier_2_cout), .b(multiplexer_3_out), .out(subtractor_4_out));  // open: bin, bout
  Multiplexer #(.width(4), .enable("false")) multiplexer_4 (
    .in0(4'b0000), .in1(in_6), .out(multiplexer_4_out), .sel(in_7[3]));
  Subtractor #(.width(4)) subtractor_5 (.a(subtractor_4_out), .b(multiplexer_4_out), .out(out_12));  // open: bin, bout
  Divider #(.width(32)) divider_1 (.a(A), .b(B), .out(divOut), .rem(remOut));  // open: upper
  Multiplier #(.width(32)) multiplier_4 (.a(A), .b(B), .out(multOut), .cout(mulhuOut));  // open: cin
  Subtractor #(.width(32)) subtractor_6 (.a(A), .b(B), .out(subOut));  // open: bin, bout
  Multiplexer #(.select(4), .width(32), .enable("false")) multiplexer_5 (
    .in0(add), .in1(andOut), .in2(orOut), .in3(xorOut), .in4(rshiftOut), .in5(rashiftOut), .in6(lshiftOut),
    .in7(sltOut), .in8(divOut), .in9(remOut), .in10(multOut), .in11(mulhuOut), .in12(subOut), .in13(B),
    .in14(mulhOut), .out(Result), .sel(ALUSel));  // open: in15

  // Other names for the same wires on the sheet: aMSB = A[31]; bMSB = B[31]; x[3:0] = in_6; xMSB = in_6[3];
  //   y[3:0] = in_7; yMSB = in_7[3]

  // Notes on the sheet:
  //   INPUTS to your circuit
  //   DON'T CHANGE THE LOCATIONS OF THE INPUTS AND OUTPUTS!
  //   OUTPUT from your circuit
endmodule

module shift (
  input  [31:0] in_1,
  input  [31:0] in_2,
  input  in_3,
  output [31:0] out_4
);

  wire io0, io1, io2, io3, io4, io5, io6, io7, io8, io9, io10, io11, io12, io13, io14, io15, io16, io17,
       io18, io19, io20, io21, io22, io23, io24, io25, io26, io27, io28, io29, io30, io31, ip0, ip1, ip2,
       ip3, ip4, ip5, ip6, ip7, ip8, ip9, ip10, ip11, ip12, ip13, ip14, ip15, ip16, ip17, ip18, ip19, ip20,
       ip21, ip22, ip23, ip24, ip25, ip26, ip27, ip28, ip29, ip30, ip31, iq0, iq1, iq2, iq3, iq4, iq5, iq6,
       iq7, iq8, iq9, iq10, iq11, iq12, iq13, iq14, iq15, iq16, iq17, iq18, iq19, iq20, iq21, iq22, iq23,
       iq24, iq25, iq26, iq27, iq28, iq29, iq30, iq31, ir0, ir1, ir2, ir3, ir4, ir5, ir6, ir7, ir8, ir9,
       ir10, ir11, ir12, ir13, ir14, ir15, ir16, ir17, ir18, ir19, ir20, ir21, ir22, ir23, ir24, ir25, ir26,
       ir27, ir28, ir29, ir30, ir31;

  Multiplexer #(.enable("false")) multiplexer_1 (.in0(in_2[31]), .in1(in_2[30]), .out(io31), .sel(in_1[0]));
  Multiplexer #(.enable("false")) multiplexer_2 (.in0(in_2[30]), .in1(in_2[29]), .out(io30), .sel(in_1[0]));
  Multiplexer #(.enable("false")) multiplexer_3 (.in0(in_2[29]), .in1(in_2[28]), .out(io29), .sel(in_1[0]));
  Multiplexer #(.enable("false")) multiplexer_4 (.in0(in_2[28]), .in1(in_2[27]), .out(io28), .sel(in_1[0]));
  Multiplexer #(.enable("false")) multiplexer_5 (.in0(in_2[27]), .in1(in_2[26]), .out(io27), .sel(in_1[0]));
  Multiplexer #(.enable("false")) multiplexer_6 (.in0(in_2[26]), .in1(in_2[25]), .out(io26), .sel(in_1[0]));
  Multiplexer #(.enable("false")) multiplexer_7 (.in0(in_2[25]), .in1(in_2[24]), .out(io25), .sel(in_1[0]));
  Multiplexer #(.enable("false")) multiplexer_8 (.in0(in_2[24]), .in1(in_2[23]), .out(io24), .sel(in_1[0]));
  Multiplexer #(.enable("false")) multiplexer_9 (.in0(in_2[23]), .in1(in_2[22]), .out(io23), .sel(in_1[0]));
  Multiplexer #(.enable("false")) multiplexer_10 (.in0(in_2[22]), .in1(in_2[21]), .out(io22), .sel(in_1[0]));
  Multiplexer #(.enable("false")) multiplexer_11 (.in0(in_2[21]), .in1(in_2[20]), .out(io21), .sel(in_1[0]));
  Multiplexer #(.enable("false")) multiplexer_12 (.in0(in_2[20]), .in1(in_2[19]), .out(io20), .sel(in_1[0]));
  Multiplexer #(.enable("false")) multiplexer_13 (.in0(in_2[19]), .in1(in_2[18]), .out(io19), .sel(in_1[0]));
  Multiplexer #(.enable("false")) multiplexer_14 (.in0(in_2[18]), .in1(in_2[17]), .out(io18), .sel(in_1[0]));
  Multiplexer #(.enable("false")) multiplexer_15 (.in0(in_2[17]), .in1(in_2[16]), .out(io17), .sel(in_1[0]));
  Multiplexer #(.enable("false")) multiplexer_16 (.in0(in_2[16]), .in1(in_2[15]), .out(io16), .sel(in_1[0]));
  Multiplexer #(.enable("false")) multiplexer_17 (.in0(in_2[15]), .in1(in_2[14]), .out(io15), .sel(in_1[0]));
  Multiplexer #(.enable("false")) multiplexer_18 (.in0(in_2[14]), .in1(in_2[13]), .out(io14), .sel(in_1[0]));
  Multiplexer #(.enable("false")) multiplexer_19 (.in0(in_2[13]), .in1(in_2[12]), .out(io13), .sel(in_1[0]));
  Multiplexer #(.enable("false")) multiplexer_20 (.in0(in_2[12]), .in1(in_2[11]), .out(io12), .sel(in_1[0]));
  Multiplexer #(.enable("false")) multiplexer_21 (.in0(in_2[11]), .in1(in_2[10]), .out(io11), .sel(in_1[0]));
  Multiplexer #(.enable("false")) multiplexer_22 (.in0(in_2[10]), .in1(in_2[9]), .out(io10), .sel(in_1[0]));
  Multiplexer #(.enable("false")) multiplexer_23 (.in0(in_2[9]), .in1(in_2[8]), .out(io9), .sel(in_1[0]));
  Multiplexer #(.enable("false")) multiplexer_24 (.in0(in_2[8]), .in1(in_2[7]), .out(io8), .sel(in_1[0]));
  Multiplexer #(.enable("false")) multiplexer_25 (.in0(in_2[7]), .in1(in_2[6]), .out(io7), .sel(in_1[0]));
  Multiplexer #(.enable("false")) multiplexer_26 (.in0(in_2[6]), .in1(in_2[5]), .out(io6), .sel(in_1[0]));
  Multiplexer #(.enable("false")) multiplexer_27 (.in0(in_2[5]), .in1(in_2[4]), .out(io5), .sel(in_1[0]));
  Multiplexer #(.enable("false")) multiplexer_28 (.in0(in_2[4]), .in1(in_2[3]), .out(io4), .sel(in_1[0]));
  Multiplexer #(.enable("false")) multiplexer_29 (.in0(in_2[3]), .in1(in_2[2]), .out(io3), .sel(in_1[0]));
  Multiplexer #(.enable("false")) multiplexer_30 (.in0(in_2[2]), .in1(in_2[1]), .out(io2), .sel(in_1[0]));
  Multiplexer #(.enable("false")) multiplexer_31 (.in0(in_2[1]), .in1(in_2[0]), .out(io1), .sel(in_1[0]));
  Multiplexer #(.enable("false")) multiplexer_32 (.in0(in_2[0]), .in1(in_3), .out(io0), .sel(in_1[0]));
  Multiplexer #(.enable("false")) multiplexer_33 (.in0(io31), .in1(io29), .out(ip31), .sel(in_1[1]));
  Multiplexer #(.enable("false")) multiplexer_34 (.in0(io30), .in1(io28), .out(ip30), .sel(in_1[1]));
  Multiplexer #(.enable("false")) multiplexer_35 (.in0(io29), .in1(io27), .out(ip29), .sel(in_1[1]));
  Multiplexer #(.enable("false")) multiplexer_36 (.in0(io28), .in1(io26), .out(ip28), .sel(in_1[1]));
  Multiplexer #(.enable("false")) multiplexer_37 (.in0(io27), .in1(io25), .out(ip27), .sel(in_1[1]));
  Multiplexer #(.enable("false")) multiplexer_38 (.in0(io26), .in1(io24), .out(ip26), .sel(in_1[1]));
  Multiplexer #(.enable("false")) multiplexer_39 (.in0(io25), .in1(io23), .out(ip25), .sel(in_1[1]));
  Multiplexer #(.enable("false")) multiplexer_40 (.in0(io24), .in1(io22), .out(ip24), .sel(in_1[1]));
  Multiplexer #(.enable("false")) multiplexer_41 (.in0(io23), .in1(io21), .out(ip23), .sel(in_1[1]));
  Multiplexer #(.enable("false")) multiplexer_42 (.in0(io22), .in1(io20), .out(ip22), .sel(in_1[1]));
  Multiplexer #(.enable("false")) multiplexer_43 (.in0(io21), .in1(io19), .out(ip21), .sel(in_1[1]));
  Multiplexer #(.enable("false")) multiplexer_44 (.in0(io20), .in1(io18), .out(ip20), .sel(in_1[1]));
  Multiplexer #(.enable("false")) multiplexer_45 (.in0(io19), .in1(io17), .out(ip19), .sel(in_1[1]));
  Multiplexer #(.enable("false")) multiplexer_46 (.in0(io18), .in1(io16), .out(ip18), .sel(in_1[1]));
  Multiplexer #(.enable("false")) multiplexer_47 (.in0(io17), .in1(io15), .out(ip17), .sel(in_1[1]));
  Multiplexer #(.enable("false")) multiplexer_48 (.in0(io16), .in1(io14), .out(ip16), .sel(in_1[1]));
  Multiplexer #(.enable("false")) multiplexer_49 (.in0(io15), .in1(io13), .out(ip15), .sel(in_1[1]));
  Multiplexer #(.enable("false")) multiplexer_50 (.in0(io14), .in1(io12), .out(ip14), .sel(in_1[1]));
  Multiplexer #(.enable("false")) multiplexer_51 (.in0(io13), .in1(io11), .out(ip13), .sel(in_1[1]));
  Multiplexer #(.enable("false")) multiplexer_52 (.in0(io12), .in1(io10), .out(ip12), .sel(in_1[1]));
  Multiplexer #(.enable("false")) multiplexer_53 (.in0(io11), .in1(io9), .out(ip11), .sel(in_1[1]));
  Multiplexer #(.enable("false")) multiplexer_54 (.in0(io10), .in1(io8), .out(ip10), .sel(in_1[1]));
  Multiplexer #(.enable("false")) multiplexer_55 (.in0(io9), .in1(io7), .out(ip9), .sel(in_1[1]));
  Multiplexer #(.enable("false")) multiplexer_56 (.in0(io8), .in1(io6), .out(ip8), .sel(in_1[1]));
  Multiplexer #(.enable("false")) multiplexer_57 (.in0(io7), .in1(io5), .out(ip7), .sel(in_1[1]));
  Multiplexer #(.enable("false")) multiplexer_58 (.in0(io6), .in1(io4), .out(ip6), .sel(in_1[1]));
  Multiplexer #(.enable("false")) multiplexer_59 (.in0(io5), .in1(io3), .out(ip5), .sel(in_1[1]));
  Multiplexer #(.enable("false")) multiplexer_60 (.in0(io4), .in1(io2), .out(ip4), .sel(in_1[1]));
  Multiplexer #(.enable("false")) multiplexer_61 (.in0(io3), .in1(io1), .out(ip3), .sel(in_1[1]));
  Multiplexer #(.enable("false")) multiplexer_62 (.in0(io2), .in1(io0), .out(ip2), .sel(in_1[1]));
  Multiplexer #(.enable("false")) multiplexer_63 (.in0(io1), .in1(in_3), .out(ip1), .sel(in_1[1]));
  Multiplexer #(.enable("false")) multiplexer_64 (.in0(io0), .in1(in_3), .out(ip0), .sel(in_1[1]));
  Multiplexer #(.enable("false")) multiplexer_65 (.in0(ip31), .in1(ip27), .out(iq31), .sel(in_1[2]));
  Multiplexer #(.enable("false")) multiplexer_66 (.in0(ip30), .in1(ip26), .out(iq30), .sel(in_1[2]));
  Multiplexer #(.enable("false")) multiplexer_67 (.in0(ip29), .in1(ip25), .out(iq29), .sel(in_1[2]));
  Multiplexer #(.enable("false")) multiplexer_68 (.in0(ip28), .in1(ip24), .out(iq28), .sel(in_1[2]));
  Multiplexer #(.enable("false")) multiplexer_69 (.in0(ip27), .in1(ip23), .out(iq27), .sel(in_1[2]));
  Multiplexer #(.enable("false")) multiplexer_70 (.in0(ip26), .in1(ip22), .out(iq26), .sel(in_1[2]));
  Multiplexer #(.enable("false")) multiplexer_71 (.in0(ip25), .in1(ip21), .out(iq25), .sel(in_1[2]));
  Multiplexer #(.enable("false")) multiplexer_72 (.in0(ip24), .in1(ip20), .out(iq24), .sel(in_1[2]));
  Multiplexer #(.enable("false")) multiplexer_73 (.in0(ip23), .in1(ip19), .out(iq23), .sel(in_1[2]));
  Multiplexer #(.enable("false")) multiplexer_74 (.in0(ip22), .in1(ip18), .out(iq22), .sel(in_1[2]));
  Multiplexer #(.enable("false")) multiplexer_75 (.in0(ip21), .in1(ip17), .out(iq21), .sel(in_1[2]));
  Multiplexer #(.enable("false")) multiplexer_76 (.in0(ip20), .in1(ip16), .out(iq20), .sel(in_1[2]));
  Multiplexer #(.enable("false")) multiplexer_77 (.in0(ip19), .in1(ip15), .out(iq19), .sel(in_1[2]));
  Multiplexer #(.enable("false")) multiplexer_78 (.in0(ip18), .in1(ip14), .out(iq18), .sel(in_1[2]));
  Multiplexer #(.enable("false")) multiplexer_79 (.in0(ip17), .in1(ip13), .out(iq17), .sel(in_1[2]));
  Multiplexer #(.enable("false")) multiplexer_80 (.in0(ip16), .in1(ip12), .out(iq16), .sel(in_1[2]));
  Multiplexer #(.enable("false")) multiplexer_81 (.in0(ip15), .in1(ip11), .out(iq15), .sel(in_1[2]));
  Multiplexer #(.enable("false")) multiplexer_82 (.in0(ip14), .in1(ip10), .out(iq14), .sel(in_1[2]));
  Multiplexer #(.enable("false")) multiplexer_83 (.in0(ip13), .in1(ip9), .out(iq13), .sel(in_1[2]));
  Multiplexer #(.enable("false")) multiplexer_84 (.in0(ip12), .in1(ip8), .out(iq12), .sel(in_1[2]));
  Multiplexer #(.enable("false")) multiplexer_85 (.in0(ip11), .in1(ip7), .out(iq11), .sel(in_1[2]));
  Multiplexer #(.enable("false")) multiplexer_86 (.in0(ip10), .in1(ip6), .out(iq10), .sel(in_1[2]));
  Multiplexer #(.enable("false")) multiplexer_87 (.in0(ip9), .in1(ip5), .out(iq9), .sel(in_1[2]));
  Multiplexer #(.enable("false")) multiplexer_88 (.in0(ip8), .in1(ip4), .out(iq8), .sel(in_1[2]));
  Multiplexer #(.enable("false")) multiplexer_89 (.in0(ip7), .in1(ip3), .out(iq7), .sel(in_1[2]));
  Multiplexer #(.enable("false")) multiplexer_90 (.in0(ip6), .in1(ip2), .out(iq6), .sel(in_1[2]));
  Multiplexer #(.enable("false")) multiplexer_91 (.in0(ip5), .in1(ip1), .out(iq5), .sel(in_1[2]));
  Multiplexer #(.enable("false")) multiplexer_92 (.in0(ip4), .in1(ip0), .out(iq4), .sel(in_1[2]));
  Multiplexer #(.enable("false")) multiplexer_93 (.in0(ip3), .in1(in_3), .out(iq3), .sel(in_1[2]));
  Multiplexer #(.enable("false")) multiplexer_94 (.in0(ip2), .in1(in_3), .out(iq2), .sel(in_1[2]));
  Multiplexer #(.enable("false")) multiplexer_95 (.in0(ip1), .in1(in_3), .out(iq1), .sel(in_1[2]));
  Multiplexer #(.enable("false")) multiplexer_96 (.in0(ip0), .in1(in_3), .out(iq0), .sel(in_1[2]));
  Multiplexer #(.enable("false")) multiplexer_97 (.in0(iq31), .in1(iq23), .out(ir31), .sel(in_1[3]));
  Multiplexer #(.enable("false")) multiplexer_98 (.in0(iq30), .in1(iq22), .out(ir30), .sel(in_1[3]));
  Multiplexer #(.enable("false")) multiplexer_99 (.in0(iq29), .in1(iq21), .out(ir29), .sel(in_1[3]));
  Multiplexer #(.enable("false")) multiplexer_100 (.in0(iq28), .in1(iq20), .out(ir28), .sel(in_1[3]));
  Multiplexer #(.enable("false")) multiplexer_101 (.in0(iq27), .in1(iq19), .out(ir27), .sel(in_1[3]));
  Multiplexer #(.enable("false")) multiplexer_102 (.in0(iq26), .in1(iq18), .out(ir26), .sel(in_1[3]));
  Multiplexer #(.enable("false")) multiplexer_103 (.in0(iq25), .in1(iq17), .out(ir25), .sel(in_1[3]));
  Multiplexer #(.enable("false")) multiplexer_104 (.in0(iq24), .in1(iq16), .out(ir24), .sel(in_1[3]));
  Multiplexer #(.enable("false")) multiplexer_105 (.in0(iq23), .in1(iq15), .out(ir23), .sel(in_1[3]));
  Multiplexer #(.enable("false")) multiplexer_106 (.in0(iq22), .in1(iq14), .out(ir22), .sel(in_1[3]));
  Multiplexer #(.enable("false")) multiplexer_107 (.in0(iq21), .in1(iq13), .out(ir21), .sel(in_1[3]));
  Multiplexer #(.enable("false")) multiplexer_108 (.in0(iq20), .in1(iq12), .out(ir20), .sel(in_1[3]));
  Multiplexer #(.enable("false")) multiplexer_109 (.in0(iq19), .in1(iq11), .out(ir19), .sel(in_1[3]));
  Multiplexer #(.enable("false")) multiplexer_110 (.in0(iq18), .in1(iq10), .out(ir18), .sel(in_1[3]));
  Multiplexer #(.enable("false")) multiplexer_111 (.in0(iq17), .in1(iq9), .out(ir17), .sel(in_1[3]));
  Multiplexer #(.enable("false")) multiplexer_112 (.in0(iq16), .in1(iq8), .out(ir16), .sel(in_1[3]));
  Multiplexer #(.enable("false")) multiplexer_113 (.in0(iq15), .in1(iq7), .out(ir15), .sel(in_1[3]));
  Multiplexer #(.enable("false")) multiplexer_114 (.in0(iq14), .in1(iq6), .out(ir14), .sel(in_1[3]));
  Multiplexer #(.enable("false")) multiplexer_115 (.in0(iq13), .in1(iq5), .out(ir13), .sel(in_1[3]));
  Multiplexer #(.enable("false")) multiplexer_116 (.in0(iq12), .in1(iq4), .out(ir12), .sel(in_1[3]));
  Multiplexer #(.enable("false")) multiplexer_117 (.in0(iq11), .in1(iq3), .out(ir11), .sel(in_1[3]));
  Multiplexer #(.enable("false")) multiplexer_118 (.in0(iq10), .in1(iq2), .out(ir10), .sel(in_1[3]));
  Multiplexer #(.enable("false")) multiplexer_119 (.in0(iq9), .in1(iq1), .out(ir9), .sel(in_1[3]));
  Multiplexer #(.enable("false")) multiplexer_120 (.in0(iq8), .in1(iq0), .out(ir8), .sel(in_1[3]));
  Multiplexer #(.enable("false")) multiplexer_121 (.in0(iq7), .in1(in_3), .out(ir7), .sel(in_1[3]));
  Multiplexer #(.enable("false")) multiplexer_122 (.in0(iq6), .in1(in_3), .out(ir6), .sel(in_1[3]));
  Multiplexer #(.enable("false")) multiplexer_123 (.in0(iq5), .in1(in_3), .out(ir5), .sel(in_1[3]));
  Multiplexer #(.enable("false")) multiplexer_124 (.in0(iq4), .in1(in_3), .out(ir4), .sel(in_1[3]));
  Multiplexer #(.enable("false")) multiplexer_125 (.in0(iq3), .in1(in_3), .out(ir3), .sel(in_1[3]));
  Multiplexer #(.enable("false")) multiplexer_126 (.in0(iq2), .in1(in_3), .out(ir2), .sel(in_1[3]));
  Multiplexer #(.enable("false")) multiplexer_127 (.in0(iq1), .in1(in_3), .out(ir1), .sel(in_1[3]));
  Multiplexer #(.enable("false")) multiplexer_128 (.in0(iq0), .in1(in_3), .out(ir0), .sel(in_1[3]));
  Multiplexer #(.enable("false")) multiplexer_129 (.in0(ir31), .in1(ir15), .out(out_4[31]), .sel(in_1[4]));
  Multiplexer #(.enable("false")) multiplexer_130 (.in0(ir30), .in1(ir14), .out(out_4[30]), .sel(in_1[4]));
  Multiplexer #(.enable("false")) multiplexer_131 (.in0(ir29), .in1(ir13), .out(out_4[29]), .sel(in_1[4]));
  Multiplexer #(.enable("false")) multiplexer_132 (.in0(ir28), .in1(ir12), .out(out_4[28]), .sel(in_1[4]));
  Multiplexer #(.enable("false")) multiplexer_133 (.in0(ir27), .in1(ir11), .out(out_4[27]), .sel(in_1[4]));
  Multiplexer #(.enable("false")) multiplexer_134 (.in0(ir26), .in1(ir10), .out(out_4[26]), .sel(in_1[4]));
  Multiplexer #(.enable("false")) multiplexer_135 (.in0(ir25), .in1(ir9), .out(out_4[25]), .sel(in_1[4]));
  Multiplexer #(.enable("false")) multiplexer_136 (.in0(ir24), .in1(ir8), .out(out_4[24]), .sel(in_1[4]));
  Multiplexer #(.enable("false")) multiplexer_137 (.in0(ir23), .in1(ir7), .out(out_4[23]), .sel(in_1[4]));
  Multiplexer #(.enable("false")) multiplexer_138 (.in0(ir22), .in1(ir6), .out(out_4[22]), .sel(in_1[4]));
  Multiplexer #(.enable("false")) multiplexer_139 (.in0(ir21), .in1(ir5), .out(out_4[21]), .sel(in_1[4]));
  Multiplexer #(.enable("false")) multiplexer_140 (.in0(ir20), .in1(ir4), .out(out_4[20]), .sel(in_1[4]));
  Multiplexer #(.enable("false")) multiplexer_141 (.in0(ir19), .in1(ir3), .out(out_4[19]), .sel(in_1[4]));
  Multiplexer #(.enable("false")) multiplexer_142 (.in0(ir18), .in1(ir2), .out(out_4[18]), .sel(in_1[4]));
  Multiplexer #(.enable("false")) multiplexer_143 (.in0(ir17), .in1(ir1), .out(out_4[17]), .sel(in_1[4]));
  Multiplexer #(.enable("false")) multiplexer_144 (.in0(ir16), .in1(ir0), .out(out_4[16]), .sel(in_1[4]));
  Multiplexer #(.enable("false")) multiplexer_145 (.in0(ir15), .in1(in_3), .out(out_4[15]), .sel(in_1[4]));
  Multiplexer #(.enable("false")) multiplexer_146 (.in0(ir14), .in1(in_3), .out(out_4[14]), .sel(in_1[4]));
  Multiplexer #(.enable("false")) multiplexer_147 (.in0(ir13), .in1(in_3), .out(out_4[13]), .sel(in_1[4]));
  Multiplexer #(.enable("false")) multiplexer_148 (.in0(ir12), .in1(in_3), .out(out_4[12]), .sel(in_1[4]));
  Multiplexer #(.enable("false")) multiplexer_149 (.in0(ir11), .in1(in_3), .out(out_4[11]), .sel(in_1[4]));
  Multiplexer #(.enable("false")) multiplexer_150 (.in0(ir10), .in1(in_3), .out(out_4[10]), .sel(in_1[4]));
  Multiplexer #(.enable("false")) multiplexer_151 (.in0(ir9), .in1(in_3), .out(out_4[9]), .sel(in_1[4]));
  Multiplexer #(.enable("false")) multiplexer_152 (.in0(ir8), .in1(in_3), .out(out_4[8]), .sel(in_1[4]));
  Multiplexer #(.enable("false")) multiplexer_153 (.in0(ir7), .in1(in_3), .out(out_4[7]), .sel(in_1[4]));
  Multiplexer #(.enable("false")) multiplexer_154 (.in0(ir6), .in1(in_3), .out(out_4[6]), .sel(in_1[4]));
  Multiplexer #(.enable("false")) multiplexer_155 (.in0(ir5), .in1(in_3), .out(out_4[5]), .sel(in_1[4]));
  Multiplexer #(.enable("false")) multiplexer_156 (.in0(ir4), .in1(in_3), .out(out_4[4]), .sel(in_1[4]));
  Multiplexer #(.enable("false")) multiplexer_157 (.in0(ir3), .in1(in_3), .out(out_4[3]), .sel(in_1[4]));
  Multiplexer #(.enable("false")) multiplexer_158 (.in0(ir2), .in1(in_3), .out(out_4[2]), .sel(in_1[4]));
  Multiplexer #(.enable("false")) multiplexer_159 (.in0(ir1), .in1(in_3), .out(out_4[1]), .sel(in_1[4]));
  Multiplexer #(.enable("false")) multiplexer_160 (.in0(ir0), .in1(in_3), .out(out_4[0]), .sel(in_1[4]));

  // Other names for the same wires on the sheet: s0 = in_1[0]; s1 = in_1[1]; s2 = in_1[2]; s3 = in_1[3]; s4 = in_1[4];
  //   in0 = in_2[0]; in1 = in_2[1]; in2 = in_2[2]; in3 = in_2[3]; in4 = in_2[4]; in5 = in_2[5]; in6 = in_2[6];
  //   in7 = in_2[7]; in8 = in_2[8]; in9 = in_2[9]; in10 = in_2[10]; in11 = in_2[11]; in12 = in_2[12]; in13 = in_2[13];
  //   in14 = in_2[14]; in15 = in_2[15]; in16 = in_2[16]; in17 = in_2[17]; in18 = in_2[18]; in19 = in_2[19];
  //   in20 = in_2[20]; in21 = in_2[21]; in22 = in_2[22]; in23 = in_2[23]; in24 = in_2[24]; in25 = in_2[25];
  //   in26 = in_2[26]; in27 = in_2[27]; in28 = in_2[28]; in29 = in_2[29]; in30 = in_2[30]; in31 = in_2[31];
  //   is0 = out_4[0]; is1 = out_4[1]; is2 = out_4[2]; is3 = out_4[3]; is4 = out_4[4]; is5 = out_4[5]; is6 = out_4[6];
  //   is7 = out_4[7]; is8 = out_4[8]; is9 = out_4[9]; is10 = out_4[10]; is11 = out_4[11]; is12 = out_4[12];
  //   is13 = out_4[13]; is14 = out_4[14]; is15 = out_4[15]; is16 = out_4[16]; is17 = out_4[17]; is18 = out_4[18];
  //   is19 = out_4[19]; is20 = out_4[20]; is21 = out_4[21]; is22 = out_4[22]; is23 = out_4[23]; is24 = out_4[24];
  //   is25 = out_4[25]; is26 = out_4[26]; is27 = out_4[27]; is28 = out_4[28]; is29 = out_4[29]; is30 = out_4[30];
  //   is31 = out_4[31]; sb = in_3
endmodule

module reverse (
  input  [31:0] in_1,
  output [31:0] out_2
);


  assign out_2 = {in_1[0], in_1[1], in_1[2], in_1[3], in_1[4], in_1[5], in_1[6], in_1[7], in_1[8], in_1[9], in_1[10], in_1[11], in_1[12], in_1[13], in_1[14], in_1[15], in_1[16], in_1[17], in_1[18], in_1[19], in_1[20], in_1[21], in_1[22], in_1[23], in_1[24], in_1[25], in_1[26], in_1[27], in_1[28], in_1[29], in_1[30], in_1[31]};

  // Other names for the same wires on the sheet: in24 = in_1[24]; in25 = in_1[25]; in26 = in_1[26]; in27 = in_1[27];
  //   in28 = in_1[28]; in29 = in_1[29]; in30 = in_1[30]; in31 = in_1[31]; in23 = in_1[23]; in22 = in_1[22];
  //   in21 = in_1[21]; in20 = in_1[20]; in19 = in_1[19]; in18 = in_1[18]; in17 = in_1[17]; in16 = in_1[16];
  //   in15 = in_1[15]; in14 = in_1[14]; in13 = in_1[13]; in12 = in_1[12]; in11 = in_1[11]; in10 = in_1[10];
  //   in9 = in_1[9]; in8 = in_1[8]; in7 = in_1[7]; in6 = in_1[6]; in5 = in_1[5]; in4 = in_1[4]; in3 = in_1[3];
  //   in2 = in_1[2]; in1 = in_1[1]; in0 = in_1[0]
endmodule
