// Logisim project cpu.circ as structural Verilog: 3 circuits, main circuit main
module main (
  input  [31:0] INSTRUCTION,
  input  CLOCK,
  output [31:0] FETCH_ADDRESS,
  output [31:0] ra,
  output [31:0] sp,
  output [31:0] t0,
  output [31:0] t1,
  output [31:0] t2,
  output [31:0] s0,
  output [31:0] s1,
  output [31:0] a0
);

  wire ALUSrcCtl, BranchCtl, MemReadCtl, MemToRegCtl, MemWriteCtl, RegWriteCtl;
  wire [3:0] ALUSelCtl;
  wire [31:0] adder_1_out, ALUOut, DMEM_p5, ImmOut, InstStage2, multiplexer_1_out, R2Data,
       RegFile_read_data_1, WBOut;

  Adder #(.width(32)) adder_1 (.a(FETCH_ADDRESS), .b(32'h1), .out(adder_1_out));  // open: cin, cout
  Register #(.width(32)) PC (.D(adder_1_out), .clk(CLOCK), .Q(FETCH_ADDRESS));  // open: en, clr
  imm imm_1 (.Inst(InstStage2), .ImmOut(ImmOut));
  Register #(.width(32)) register_1 (.D(INSTRUCTION), .en(1'b1), .clk(CLOCK), .Q(InstStage2));  // open: clr
  regfile_main RegFile (
    .rs2(InstStage2[24:20]), .rd(InstStage2[11:7]), .Read_Data_1(RegFile_read_data_1), .Read_Data_2(R2Data),
    .ra(ra), .sp(sp), .t0(t0), .t1(t1), .t2(t2), .s0(s0), .s1(s1), .a0(a0), .rs1(InstStage2[19:15]),
    .Write_Data(WBOut), .RegWEn(RegWriteCtl), .clk(CLOCK));
  Multiplexer #(.width(32), .enable("false")) multiplexer_1 (
    .in0(R2Data), .in1(ImmOut), .out(multiplexer_1_out), .sel(ALUSrcCtl));
  alu Arithmetic_Logic_Unit (.A(RegFile_read_data_1), .B(multiplexer_1_out), .ALUSel(ALUSelCtl), .Result(ALUOut));
  control control_1 (
    .Inst(InstStage2), .BranchCtl(BranchCtl), .MemReadCtl(MemReadCtl), .MemToRegCtl(MemToRegCtl),
    .MemWriteCtl(MemWriteCtl), .ALUSelCtl(ALUSelCtl), .ALUSrcCtl(ALUSrcCtl), .RegWriteCtl(RegWriteCtl));
  // mem_main DMEM: pin names not known; wires that end beside it: ALUOut, R2Data, MemWriteCtl, CLOCK, DMEM_p5
  Multiplexer #(.width(32), .enable("false")) multiplexer_2 (
    .in0(DMEM_p5), .in1(ALUOut), .out(WBOut), .sel(MemToRegCtl));

  // Other names for the same wires on the sheet: clk = CLOCK; fetch_addr[31:0] = FETCH_ADDRESS;
  //   WriteReg[4:0] = InstStage2[11:7]

  // Notes on the sheet:
  //   Output
  //   Inputs/Outputs from run.circ. DO NOT MOVE THESE.
  //   Inputs
  //   It is OK to move the PC, RegFile, ALU, and MEM to wherever is most convenient for you when constructing your CPU, and to delete this text
  //   Inputs/Outputs from run.circ. DO NOT MOVE THESE.
endmodule

module imm (
  input  [31:0] Inst,
  output [31:0] ImmOut
);

  wire [3:0] ImmROM_data;
  wire [31:0] Bimm, Iimm, Jimm, Simm;

  assign Simm = {{20{Inst[31]}}, {Inst[31:25], Inst[11:7]}};  // Bit_Extender bit_extender_1
  assign Bimm = {{19{Inst[31]}}, {Inst[31], Inst[7], Inst[30:25], Inst[11:8], 1'b0}};  // Bit_Extender bit_extender_2
  ROM #(.addrWidth(7), .dataWidth(4)) ImmROM (.addr(Inst[6:0]), .data(ImmROM_data));
  assign Jimm = {{11{Inst[31]}}, {Inst[31], Inst[19:12], Inst[20], Inst[30:21], 1'b0}};  // Bit_Extender bit_extender_3
  Multiplexer #(.select(4), .width(32), .enable("false")) multiplexer_1 (
    .in0(Iimm), .in1(Simm), .in2(Bimm), .in3({Inst[31:12], {12{1'b0}}}), .in4(Jimm), .out(ImmOut),
    .sel(ImmROM_data));  // open: in5, in6, in7, in8, in9, in10, in11, in12, in13, in14, in15
  assign Iimm = {{20{Inst[31]}}, Inst[31:20]};  // Bit_Extender bit_extender_4

  // Other names for the same wires on the sheet: instruction[31:0] = Inst; bit7 = Inst[7];
  //   bit12_15[3:0] = Inst[15:12]; Uimm[31:12] = Inst[31:12]; bit16_19[3:0] = Inst[19:16]; bit20 = Inst[20];
  //   bit31 = Inst[31]; opcode[6:0] = Inst[6:0]

  // Notes on the sheet:
  //   contents of ImmROM (hex, n*v repeats v):
  //   35*0 1 19*0 3 43*0 2 11*0 4
endmodule

module control (
  input  [31:0] Inst,
  output BranchCtl,
  output MemReadCtl,
  output MemToRegCtl,
  output MemWriteCtl,
  output [3:0] ALUSelCtl,
  output ALUSrcCtl,
  output RegWriteCtl
);

  wire [15:10] ControlROM_data;

  ROM #(.addrWidth(10), .dataWidth(16)) ControlROM (
    .addr({Inst[30], Inst[25], Inst[14:12], Inst[6:2]}),
    .data({ControlROM_data, RegWriteCtl, ALUSrcCtl, ALUSelCtl, MemWriteCtl, MemToRegCtl, MemReadCtl, BranchCtl}));

  // Other names for the same wires on the sheet: instruction[31:0] = Inst

  // Notes on the sheet:
  //   contents of ControlROM (hex, n*v repeats v):
  //   12*0 204 6*0 304 8*0 214 15*0 264 31*0 274 63*0 234 31*0 244 31*0 224 23*0 304 39*0 2a4 6*0 304 8*0
  //   294 15*0 2e4 63*0 2b4 63*0 284 95*0 2c4 6*0 304 255*0 304
endmodule
